# Fritzing sketch LED-MOSFET-Bueno (saved by Fritzing 0.9.2b)
breadboards: 1

parts:
  Parte1 = Arduino Uno (Rev3) - ICSP
  JACK1 = 2.1mm Barrel Jack with Terminal Block
  Q1 = Basic FET N-Channel [package="TO220 [THT]"]
  LED1 = LED - 3mm [color="Red (633nm)" package="3 mm [THT]"]
  R1 = Resistor [tolerance=±5% resistance=220 package=THT]

nets:
  N1: Parte1.GND, JACK1.NEG, Q1.source
  N2: Parte1.D3_PWM, Q1.gate
  N3: JACK1.POS, R1.Pin_1
  N4: Q1.drain, LED1.cathode
  N5: LED1.anode, R1.Pin_0
